# Fritzing sketch nrf24_led_ring_o2Gij5oigT (saved by Fritzing 0.9.3b)

parts:
  Part1 = 12 NeoPixel Ring [part_number=1643]
  Nano1 = Arduino Nano v2.3
  Part2 = NRF24L01+ Breakout Board
  U1 = LIPO-110mAh [package=lipo-110]

nets:
  N1: Part1.IN, Nano1.D5
  VDD: Part1.VDD, Nano1.+5V, U1.+
  GND: Part1.GND, Nano1.GND, Part2.GND, U1.-
  N2: Nano1.D8, Part2.CS
  N3: Nano1.D9, Part2.CE
  N4: Nano1.D11, Part2.MOSI
  N5: Nano1.D12, Part2.MISO
  N6: Nano1.D13, Part2.SCK
  3V3: Nano1.3V3, Part2.VCC

custom parts:
  12 NeoPixel Ring: 12 ultra bright smart LED NeoPixels are arranged in a circle with 1.5" (37mm) outer diameter. The rings are 'chainable' - connect the output pin of one to the input pin of another. Use only one microcontroller pin to control as many as you can chain together! Each LED is addressable as the driver chip is inside the LED. Each one has ~18mA constant current drive so the color will be very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
